# Fritzing sketch atmega8_burn (saved by Fritzing 0.9.3b)
breadboards: 1

parts:
  J1 = AVR ISP 6 Pin [package=2x3-ns]
  IC2 = ATMEGA8 [package=DIL]
  XTAL2 = Crystal [frequency="16 Mhz" package=THT]

nets:
  N1: J1.1, IC2.PB4
  N2: J1.2, IC2.VCC
  N3: J1.3, IC2.PB5
  N4: J1.4, IC2.PB3
  N5: J1.5, IC2.PC6
  N6: J1.6, IC2.GND#8
  N7: IC2.PB6, XTAL2.pin_1
  N8: IC2.PB7, XTAL2.pin_0

notes:
  MOSI
  MISO
  RESET
  GND
  VCC
  SCK
