# Fritzing sketch atmega8_mmml (saved by Fritzing 0.9.3b)
breadboards: 1

parts:
  IC1 = MICROCONTROLLER [package=dil28-3-zif_socket]
  Composant1 = Arduino Nano (Rev3.0)
  SP1 = SPEAKER [package=pcb_mount_speaker]

nets:
  VCC: IC1.VCC, Composant1.5V
  GND: IC1.GND, Composant1.GND
  N1: IC1.PB0(ICP), SP1.-
  N2: IC1.AGND, SP1.+
