# Fritzing sketch expansion_board (saved by Fritzing 0.9.3b)
circuit board: 8cm x 3.5cm
breadboards: 1

parts:
  U2 = POT [package=pot_alpha_rv16af-20]
  U3 = POT [package=pot_alpha_rv16af-20]
  U1 = POT [package=pot_alpha_rv16af-20]
  U4 = POT [package=pot_alpha_rv16af-20]
  U5 = POT [package=pot_alpha_rv16af-20]
  -_+ = male pin header, 2 pins [form="♂ (male)"]
  Sw1 = Momentary Switch [package=ksa_sealed_tac_switch]
  Sw2 = Momentary Switch [package=ksa_sealed_tac_switch]
  J1 = male pin header, 4 pins [form="♂ (male)"]
  J2 = male pin header, 3 pins [form="♂ (male)"]
  Sw3 = Momentary Switch [package=ksa_sealed_tac_switch]
  Sw4 = Momentary Switch [package=ksa_sealed_tac_switch]
  Sw5 = Momentary Switch [package=ksa_sealed_tac_switch]
  TRS2 = Audio Jack (TRS) 3.5mm [package="4Ucon 08780 [THT]"]
  J4 = male pin header, 2 pins [form="♂ (male)"]
  J3 = male pin header, 5 pins [form="♂ (male)"]

nets:
  N1: U2.A, U3.A, U1.A, U4.A, U5.A, -_+.pin2, Sw1.1, Sw1.2, Sw2.1, Sw2.2, Sw3.1, Sw3.2, Sw4.1, Sw4.2, Sw5.1, Sw5.2, TRS2.Sleeve, J4.pin1
  N2: U2.S, J2.pin2
  N3: U2.E, U3.E, U1.E, U4.E, U5.E, -_+.pin1
  N4: U3.S, J2.pin1
  N5: U1.S, J2.pin3
  N6: U4.S, J1.pin1
  N7: U5.S, J1.pin2
  N8: Sw1.3, Sw1.4, J1.pin4
  N9: Sw2.3, Sw2.4, J1.pin3
  N10: Sw3.3, Sw3.4, J3.pin5
  N11: Sw4.3, Sw4.4, J3.pin4
  N12: Sw5.3, Sw5.4, J3.pin3
  N13: TRS2.Ring, TRS2.Tip, J3.pin1

notes:
  garvalf.online.fr
  expansion board v2.11
  GARVUINO expansion board v2.10 / 2018-02
