# Fritzing sketch garvuino_09g (saved by Fritzing 0.9.3b)
circuit board: 8cm x 7cm
breadboards: 2

parts:
  24_Mhz = Crystal [frequency="25 MHz" package=THT]
  Arduino_Nano = Arduino Nano (Rev3.0)
  R4 = Resistor [tolerance=±5% resistance=10k package=THT]
  C6 = Electrolytic Capacitor [capacitance=10µF package="100 mil [THT, electrolytic]"]
  R5 = Resistor [tolerance=±5% resistance=10k package=THT]
  C3 = Electrolytic Capacitor [capacitance=10µF package="100 mil [THT, electrolytic]"]
  C2 = Ceramic Capacitor [capacitance=820pF voltage=6.3V package="100 mil [THT, multilayer]"]
  C7 = Ceramic Capacitor [capacitance=820pF voltage=6.3V package="100 mil [THT, multilayer]"]
  Switch = Momentary Switch [package=ksa_sealed_tac_switch]
  midi = MIDI_CONN_FEMALE_SUPPORT [package=din_5_female_support]
  TRS = Audio Jack (TRS) 3.5mm [package="4Ucon 08780 [THT]"]
  J1 = male pin header, 2 pins [form="♂ (male)"]
  J2 = male pin header, 8 pins [form="♂ (male)"]
  J3 = male pin header, 8 pins [form="♂ (male)"]
  J4 = male pin header, 3 pins [form="♂ (male)"]
  LED1 = LED - 5mm [color="Red (633nm)" package="5 mm [THT]"]
  R3 = Resistor [tolerance=±5% resistance=1k package=THT]
  J5 = male pin header, 1 pin [form="♂ (male)"]
  Atmega8 = MICROCONTROLLER [package=dil28-3-simon-kit]
  mono = male pin header, 2 pins [form="♂ (male)"]
  J8 = male pin header, 4 pins [form="♂ (male)"]
  C5 = Ceramic Capacitor [capacitance=100nF package="100 mil [THT, multilayer]"]
  J6 = male pin header, 3 pins [form="♂ (male)"]
  sd = MicroSD Card Module
  TX = male pin header, 2 pins [form="♂ (male)"]
  J9 = male pin header, 4 pins [form="♂ (male)"]
  AY>L = male pin header, 2 pins [form="♂ (male)"]
  AY>R = male pin header, 2 pins [form="♂ (male)"]
  J10 = male pin header, 1 pin [form="♂ (male)"]
  J7 = male pin header, 6 pins [form="♂ (male)"]

nets:
  N1: 24_Mhz.pin_0, Atmega8.PB6(XTAL1_TOSC1)
  N2: 24_Mhz.pin_1, Atmega8.PB7(XTAL2_TOSC2)
  N3: Arduino_Nano.D1/TX, TX.pin2
  N4: Arduino_Nano.D0/RX, midi.MIDI_IN, J1.pin2
  N5: Arduino_Nano.GND, C2.0, C7.0, Switch.1, midi.NC1, TRS.Sleeve, J1.pin1, J2.pin1, J4.pin1, LED1.cathode, J8.pin2
  N6: Arduino_Nano.D4, J2.pin4, J3.pin5, sd.CS, J9.pin1
  N7: Arduino_Nano.D5, J9.pin2
  N8: Arduino_Nano.D6, J9.pin3
  N9: Arduino_Nano.D7, J9.pin4
  N10: Arduino_Nano.D8, Switch.3, R3.Pin_1
  N11: Arduino_Nano.D9, R5.Pin_1, AY>L.pin1
  N12: Arduino_Nano.D10, J10.pin1
  N13: Arduino_Nano.D11/MOSI, J2.pin5, J3.pin4, sd.MOSI
  N14: Arduino_Nano.D12/MISO, J2.pin7, J3.pin2, sd.MISO
  N15: Arduino_Nano.VIN, J8.pin1
  5V: Arduino_Nano.5V, J2.pin3, J8.pin4, J6.pin2, sd.VCC
  N16: Arduino_Nano.A5, J7.pin1
  N17: Arduino_Nano.A4, J7.pin2
  N18: Arduino_Nano.A3, J7.pin3
  N19: Arduino_Nano.A2, J7.pin4
  N20: Arduino_Nano.A1, J7.pin5
  N21: Arduino_Nano.A0, J7.pin6
  N22: Arduino_Nano.D13/SCK, J2.pin6, J3.pin3, sd.SCK
  N23: R4.Pin_0, C6.+, C2.1
  N24: R4.Pin_1, AY>R.pin1
  N25: C6.-, TRS.Ring, mono.pin1
  N26: R5.Pin_0, C3.+, C7.1
  N27: C3.-, TRS.Tip, mono.pin2
  N28: midi.MIDI_OUT, J5.pin1
  GND: J4.pin2, Atmega8.GND, C5.0, sd.GND
  N29: LED1.anode, R3.Pin_0
  N30: Atmega8.PD0(RXD), TX.pin1
  N31: Atmega8.VCC, C5.1, J6.pin3
  N32: Atmega8.PB1(OC1A), AY>L.pin2
  N33: Atmega8.PB2(SS_OC1B), AY>R.pin2

notes:
  GARVUINO chiptune player v1.09 / 2017-08
  chiptune player v1.09
  midi
  ay chip GND
  arduino chip
  mini usb
  www.avray.ru
  garvalf.online.fr
  GND
  5V
  CS
  MOSI
  SCK
  MISO
  SD card reader
  R
  L
  Mozzi 8-bit
  AVR-AY 8-bit
  Beeper 1-bit
  SID 8-bit
