# Fritzing sketch garvuino_10p (saved by Fritzing 0.9.3b)
circuit board: 8cm x 7cm
breadboards: 2

parts:
  24_Mhz = Crystal [frequency="25 MHz" package=THT]
  Arduino_Nano = Arduino Nano (Rev3.0)
  R4 = Resistor [tolerance=±5% resistance=10k package=THT]
  C6 = Electrolytic Capacitor [capacitance=10µF package="100 mil [THT, electrolytic]"]
  R5 = Resistor [tolerance=±5% resistance=10k package=THT]
  C3 = Electrolytic Capacitor [capacitance=10µF package="100 mil [THT, electrolytic]"]
  C2 = Ceramic Capacitor [capacitance=820pF voltage=6.3V package="100 mil [THT, multilayer]"]
  C7 = Ceramic Capacitor [capacitance=820pF voltage=6.3V package="100 mil [THT, multilayer]"]
  midi = MIDI_CONN_FEMALE_SUPPORT [package=din_5_female_support]
  TRS = Audio Jack (TRS) 3.5mm [package="4Ucon 08780 [THT]"]
  J1 = male pin header, 2 pins [form="♂ (male)"]
  LED1 = LED - 5mm [color="Red (633nm)" package="5 mm [THT]"]
  R3 = Resistor [tolerance=±5% resistance=1k package=THT]
  J5 = male pin header, 1 pin [form="♂ (male)"]
  Atmega8 = MICROCONTROLLER [package=dil28-3-simon-kit]
  mono = male pin header, 2 pins [form="♂ (male)"]
  J8 = male pin header, 4 pins [form="♂ (male)"]
  C5 = Ceramic Capacitor [capacitance=100nF package="100 mil [THT, multilayer]"]
  sd = MicroSD Card Module
  TX = male pin header, 2 pins [form="♂ (male)"]
  AY>L = male pin header, 2 pins [form="♂ (male)"]
  AY>R = male pin header, 2 pins [form="♂ (male)"]
  J10 = male pin header, 1 pin [form="♂ (male)"]
  J7 = male pin header, 6 pins [form="♂ (male)"]
  J9 = male pin header, 6 pins [form="♂ (male)"]
  U1 = POT [package=pot_alpha_rv16af-20]
  U2 = POT [package=pot_alpha_rv16af-20]
  Sw2 = Momentary Switch [package=ksa_sealed_tac_switch]
  J11 = male pin header, 3 pins [form="♂ (male)"]
  J12 = male pin header, 1 pin [form="♂ (male)"]  # not connected
  Sw3 = Momentary Switch [package=ksa_sealed_tac_switch]
  Sw1 = Momentary Switch [package=ksa_sealed_tac_switch]

nets (from the pcb view):
  N1: 24_Mhz.pin_0, Atmega8.PB6(XTAL1_TOSC1)
  N2: 24_Mhz.pin_1, Atmega8.PB7(XTAL2_TOSC2)
  N3: Arduino_Nano.D1/TX, TX.pin2
  N4: Arduino_Nano.D0/RX, midi.MIDI_IN, J1.pin2
  N5: Arduino_Nano.RESET, J8.pin3
  GND: Arduino_Nano.GND, C2.0, C7.0, midi.NC1, TRS.Sleeve, J1.pin1, LED1.cathode, Atmega8.GND, J8.pin2, C5.0, sd.GND, U1.A, U2.A, Sw2.1, Sw2.2, J11.pin1, Sw3.1, Sw3.2, Sw1.1, Sw1.2
  N6: Arduino_Nano.D2, J9.pin1
  N7: Arduino_Nano.D3, J9.pin2
  N8: Arduino_Nano.D4, sd.CS, J9.pin3
  N9: Arduino_Nano.D5, J9.pin4
  N10: Arduino_Nano.D6, J9.pin5, Sw1.3, Sw1.4
  N11: Arduino_Nano.D7, J9.pin6, Sw3.3, Sw3.4
  N12: Arduino_Nano.D8, R3.Pin_1
  N13: Arduino_Nano.D9, R5.Pin_1, AY>L.pin1
  N14: Arduino_Nano.D10, J10.pin1, Sw2.3, Sw2.4
  N15: Arduino_Nano.D11/MOSI, sd.MOSI
  N16: Arduino_Nano.D12/MISO, sd.MISO
  N17: Arduino_Nano.VIN, J8.pin1
  VCC: Arduino_Nano.5V, Atmega8.VCC, J8.pin4, C5.1, sd.VCC, U1.E, U2.E, J11.pin3
  N18: Arduino_Nano.A5, J7.pin1
  N19: Arduino_Nano.A4, J7.pin2
  N20: Arduino_Nano.A3, J7.pin3
  N21: Arduino_Nano.A2, J7.pin4, J11.pin2
  N22: Arduino_Nano.A1, J7.pin5, U2.S
  N23: Arduino_Nano.A0, J7.pin6, U1.S
  N24: Arduino_Nano.D13/SCK, sd.SCK
  N25: R4.Pin_0, C6.+, C2.1
  N26: R4.Pin_1, AY>R.pin1
  N27: C6.-, TRS.Ring, mono.pin1
  N28: R5.Pin_0, C3.+, C7.1
  N29: C3.-, TRS.Tip, mono.pin2
  N30: midi.MIDI_OUT, J5.pin1
  N31: LED1.anode, R3.Pin_0
  N32: Atmega8.PD0(RXD), TX.pin1
  N33: Atmega8.PB1(OC1A), AY>L.pin2
  N34: Atmega8.PB2(SS_OC1B), AY>R.pin2

notes:
  GARVUINO chiptune player v2.10 / 2018-01
  v2.10
  midi
  usb mini
  garvalf.online.fr
  www.avray.ru
  SD card reader
  GND
  R
  L
  CS
  SCK
  MISO
  MOSI
  Mozzi 8-bit
  AVR-AY 8-bit
  Beeper 1-bit
  SID 8-bit
  ➜
  VCC
